# Fritzing sketch Electronics_sketc (saved by Fritzing 1.0.6)

parts:
  XIAO_ESP32S1 = XIAO ESP32S3 [package="DIP (Dual Inline) [THT]"]
  NEOPIXEL1 = Neopixel Strip -- White (60/m) [part_number=1138]  # not connected
  X2 = USB Connectors [package=usb-a-s-nosilk-female]
  LED1 = LED - 5mm [color="Red (633nm)" current=0.030A package="5 mm [THT]"]  # not connected
  Q1 = Basic FET N-Channel [package="D2Pak [SMD]"]
  R1 = Resistor [tolerance=±5% resistance=10k package="2512 [SMD]"]
  R2 = Resistor [tolerance=±5% resistance=220 package="2512 [SMD]"]
  X3 = USB Connectors [package=usb-a-s-nosilk-female]

nets:
  N1: XIAO_ESP32S1.D5, R1.Pin_0
  N2: XIAO_ESP32S1.D6, R2.Pin_0
  GND: XIAO_ESP32S1.GND, X2.GND
  N3: X2.VBUS, X3.VBUS
  N4: Q1.Gate, R1.Pin_1
  N5: Q1.drain, X3.GND

notes:
  10K
  220 ohms
  IRL744N
  POWER
  LEDs

custom parts:
  XIAO ESP32S3: Seeed Studio XIAO ESP32S3 leverages 240MHz Xtensa 32-bit LX7 dual-core processor, supporting both WiFi and BLE 5.0 wireless connectivities, a 2.4GHz Rod antenna, allows for deep sleep mode with power consumption as low as 14μA while supporting lithium battery charging management. Ideal for the Internet of Things, Smart Homes, Wireless wearable devices, Robotics, etc.
  Neopixel Strip -- White (60/m): Neopixel Strip, White, 60 pixels per meter.
